# Fritzing sketch rpi connector (saved by Fritzing 0.9.6b)
breadboards: 1

parts:
  HC-SR04_Sensor_front = HC-SR04 Ultrasonic Distance Sensor [part_number="front sensor"]
  R1 = Resistor [tolerance=±5% resistance=1000 package="2512 [SMD]"]
  R2 = Resistor [tolerance=±5% resistance=2000 package="2512 [SMD]"]
  HC-SR04_sensor_left = HC-SR04 Ultrasonic Distance Sensor [part_number="left sensor"]
  R3 = Resistor [tolerance=±5% resistance=1000 package="2512 [SMD]"]
  R4 = Resistor [tolerance=±5% resistance=2000 package="2512 [SMD]"]
  HC-SR04_Sensor_right = HC-SR04 Ultrasonic Distance Sensor [part_number="right sensor"]
  R5 = Resistor [tolerance=±5% resistance=1000 package="2512 [SMD]"]
  R6 = Resistor [tolerance=±5% resistance=2000 package="2512 [SMD]"]
  oled_screen = Grove OLED 128x96
  rpi = Raspberry Pi 4B

nets:
  VCC: HC-SR04_Sensor_front.VCC, HC-SR04_sensor_left.VCC, HC-SR04_Sensor_right.VCC, oled_screen.VCC, rpi.5V
  N1: HC-SR04_Sensor_front.TRIG, rpi.GPIO6
  N2: HC-SR04_Sensor_front.ECHO, R1.Pin_0
  GND: HC-SR04_Sensor_front.GND, R2.Pin_0, HC-SR04_sensor_left.GND, R4.Pin_0, HC-SR04_Sensor_right.GND, R6.Pin_1, oled_screen.GND, rpi.GND
  N3: R1.Pin_1, R2.Pin_1, rpi.GPIO5
  N4: HC-SR04_sensor_left.TRIG, rpi.GPIO27
  N5: HC-SR04_sensor_left.ECHO, R3.Pin_0
  N6: R3.Pin_1, R4.Pin_1, rpi.GPIO17
  N7: HC-SR04_Sensor_right.TRIG, rpi.GPIO24
  N8: HC-SR04_Sensor_right.ECHO, R5.Pin_1
  N9: R5.Pin_0, R6.Pin_0, rpi.GPIO23
  N10: oled_screen.SDA, rpi.GPIO2
  N11: oled_screen.SCL, rpi.GPIO3
